# Fritzing sketch joystick (saved by Fritzing 0.8.7b)
breadboards: 1

parts:
  LEFT = Pushbutton [package="[THT]"]
  RIGHT = Pushbutton [package="[THT]"]
  UP = Pushbutton [package="[THT]"]
  Componente1 = Arduino Uno (Rev3)
  DOWN = Pushbutton [package="[THT]"]
  FIRE = Pushbutton [package="[THT]"]
  R3 = Resistor [tolerance=±5% resistance=10k package=THT]
  R4 = Resistor [tolerance=±5% resistance=10k package=THT]
  R5 = Resistor [tolerance=±5% resistance=10k package=THT]
  R6 = Resistor [tolerance=±5% resistance=10k package=THT]
  R7 = Resistor [tolerance=±5% resistance=10k package=THT]

nets:
  N1: LEFT.Pin_1, LEFT.Pin_2, RIGHT.Pin_1, RIGHT.Pin_2, UP.Pin_1, UP.Pin_2, Componente1.5V, DOWN.Pin_1, DOWN.Pin_2, FIRE.Pin_1, FIRE.Pin_2
  N2: LEFT.Pin_3, LEFT.Pin_4, Componente1.D11_PWM/MOSI, R6.Pin_0
  N3: RIGHT.Pin_3, RIGHT.Pin_4, Componente1.D8, R5.Pin_0
  N4: UP.Pin_3, UP.Pin_4, Componente1.D10_PWM/SS, R7.Pin_0
  N5: Componente1.D9_PWM, DOWN.Pin_3, DOWN.Pin_4, R4.Pin_0
  N6: Componente1.D12/MISO, FIRE.Pin_3, FIRE.Pin_4, R3.Pin_0
  N7: Componente1.GND, R3.Pin_1, R4.Pin_1, R5.Pin_1, R6.Pin_1, R7.Pin_1
